# Fritzing sketch PCB (saved by Fritzing 1.0.1rc)
circuit board: 8.46667cm x 6.71175cm

parts:
  5V = female pin header, 1 pin [form="♀ (female)"]
  GND = female pin header, 1 pin [form="♀ (female)"]
  STEP = female pin header, 5 pins [form="♀ (female)"]
  DIR = female pin header, 5 pins [form="♀ (female)"]
  Left = female pin header, 4 pins [form="♀ (female)"]
  Right = female pin header, 4 pins [form="♀ (female)"]
  EN/GND = female pin header, 2 pins [form="♀ (female)"]
  left_filler = female pin header, 4 pins [form="♀ (female)"]  # not connected
  J2 = female pin header, 3 pins [form="♀ (female)"]  # not connected
  J3 = female pin header, 5 pins [form="♀ (female)"]  # not connected
  J4 = female pin header, 6 pins [form="♀ (female)"]  # not connected

nets:
  N1: 5V.pin1, STEP.pin5
  N2: GND.pin1, DIR.pin5
  N3: STEP.pin1, Left.pin1
  N4: STEP.pin2, Left.pin2
  N5: STEP.pin3, Left.pin3
  N6: STEP.pin4, Left.pin4
  N7: DIR.pin1, Right.pin4
  N8: DIR.pin2, Right.pin3
  N9: DIR.pin3, Right.pin2
  N10: DIR.pin4, Right.pin1
  N11: EN/GND.pin1, EN/GND.pin2
