# Fritzing sketch Wiring (saved by Fritzing 1.0.1rc)
circuit board: 2.6cm x 5cm

parts:
  Arduino_CNC_Shield_V3_00_1 = Arduino_CNC_V3.00
  U1 = ESP32S-HiLetgo [part_number=ESP32S-HiLetgo]

nets:
  N1: Arduino_CNC_Shield_V3_00_1.EN(able), Arduino_CNC_Shield_V3_00_1.GND#2
  N2: Arduino_CNC_Shield_V3_00_1.X.STEP, U1.GPIO26
  N3: Arduino_CNC_Shield_V3_00_1.X.DIR, U1.GPIO15
  N4: Arduino_CNC_Shield_V3_00_1.Y.STEP, U1.GPIO27
  N5: Arduino_CNC_Shield_V3_00_1.Y.DIR, U1.GPIO2
  N6: Arduino_CNC_Shield_V3_00_1.Z.STEP, U1.GPIO14
  N7: Arduino_CNC_Shield_V3_00_1.Z.DIR, U1.GPIO0
  N8: Arduino_CNC_Shield_V3_00_1.A.STEP, U1.GPIO12
  N9: Arduino_CNC_Shield_V3_00_1.A.DIR, U1.GPIO4
  5V: Arduino_CNC_Shield_V3_00_1.5V, U1.VIN
  N10: Arduino_CNC_Shield_V3_00_1.GND#12, U1.GND

custom parts:
  Arduino_CNC_V3.00: Protoneer Arduino CNC Shield V3.00 If using Grbl V0.9: The “A” axis can not be used (yet). The “SCL” (Arduino A5) pin is now used for 'Probing' input. The “End Stops Z+ & Z-” (Arduino D11) and “SpnEn” (Arduino D12) have been switched!
  ESP32S-HiLetgo: HiLetgo ESP-WROOM-32 ESP32 ESP-32S Development Board 2.4GHz Dual-Mode WiFi + Bluetooth Dual Cores Microcontroller The ESP32 integrated with Antenna switches, RF Balun, power amplifiers, low-noise amplifiers, filters, and management modules, and the entire solution occupies the least area of PCB. 2.4 GHz Wi-Fi plus Bluetooth dual-mode chip, with TSMC Ultra-low power consumption 40nm technology,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
