# Fritzing sketch PCB (saved by Fritzing 1.0.1rc)
circuit board: 2.59745cm x 4.91505cm

parts:
  U1 = ESP32S-HiLetgo [part_number=ESP32S-HiLetgo]
  J2 = female pin header, 5 pins [form="♀ (female)"]
  J1 = female pin header, 4 pins [form="♀ (female)"]

nets:
  N1: U1.GPIO26, J1.pin1
  N2: U1.GPIO27, J1.pin2
  N3: U1.GPIO14, J1.pin3
  N4: U1.GPIO12, J1.pin4
  N5: U1.GPIO15, J2.pin1
  N6: U1.GPIO2, J2.pin2
  N7: U1.GPIO0, J2.pin3
  N8: U1.GPIO4, J2.pin4
  N9: U1.GND, J2.pin5

notes:
  12 A Step
  14 Z Step
  27 Y Step
  15 X Dir
  2 Y Dir
  0 Z Dir
  4 A Dir
  X Y Z A
  26 X Step
  CNC V3 ESP-WROOM-32

custom parts:
  ESP32S-HiLetgo: HiLetgo ESP-WROOM-32 ESP32 ESP-32S Development Board 2.4GHz Dual-Mode WiFi + Bluetooth Dual Cores Microcontroller The ESP32 integrated with Antenna switches, RF Balun, power amplifiers, low-noise amplifiers, filters, and management modules, and the entire solution occupies the least area of PCB. 2.4 GHz Wi-Fi plus Bluetooth dual-mode chip, with TSMC Ultra-low power consumption 40nm technology,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
